# Fritzing sketch model (saved by Fritzing 0.8.3b)
breadboards: 2

parts:
  Part1 = Arduino Uno (Rev3)
  R1 = Resistor [tolerance=±5% resistance=220 package=THT]
  R6 = Resistor [tolerance=±5% resistance=10k package=THT]
  R7 = Resistor [tolerance=±5% resistance=220 package=THT]
  R8 = Resistor [tolerance=±5% resistance=220 package=THT]
  R9 = Resistor [tolerance=±5% resistance=220 package=THT]
  R10 = Resistor [tolerance=±5% resistance=10k package=THT]
  R11 = Resistor [tolerance=±5% resistance=10k package=THT]
  R12 = Resistor [tolerance=±5% resistance=10k package=THT]
  U1 = MAX7219 [package=dil24]
  R13 = Resistor [tolerance=±5% resistance=10k package=THT]

nets:
  GND: Part1.GND, U1.GND, U1.GND2
  N1: Part1.D10_PWM/SS, U1.LOAD
  N2: Part1.D11_PWM/MOSI, U1.CLK
  N3: Part1.D12/MISO, U1.DIN
  5V: Part1.5V, U1.VCC, R13.Pin_0
  N4: R1.Pin_0, U1.SEGG
  N5: R6.Pin_0, U1.SEGDP
  N6: R7.Pin_0, U1.SEGF
  N7: R8.Pin_0, U1.SEGE
  N8: R9.Pin_0, U1.SEGD
  N9: R10.Pin_0, U1.SEGA
  N10: R11.Pin_0, U1.SEGB
  N11: R12.Pin_0, U1.SEGC
  N12: U1.ISET, R13.Pin_1
